# Fritzing sketch shema (saved by Fritzing 0.9.3b)
breadboards: 1

parts:
  MBED2 = mbed
  S1 = Pushbutton [package="[SMD]"]
  R1 = Resistor [tolerance=±5% resistance=220 package=THT]
  S2 = Pushbutton [package="[THT]"]
  R2 = Resistor [tolerance=±5% resistance=220 package=THT]
  Banggood_Display1 = Banggood Display
  Nokia_5110_LCD_Module1 = Nokia 5110 LCD

nets:
  GND: MBED2.GND, S1.Pin_3, S1.Pin_4, S2.Pin_3, S2.Pin_4, Banggood_Display1.GND, Nokia_5110_LCD_Module1.GND_(out)
  N1: MBED2.pin5, Banggood_Display1.SDO
  N2: MBED2.pin6, S2.Pin_1, S2.Pin_2, R2.Pin_0
  N3: MBED2.pin7, Banggood_Display1.SCK
  N4: MBED2.pin8, S1.Pin_1, S1.Pin_2, R1.Pin_0
  N5: MBED2.pin9, Nokia_5110_LCD_Module1.RST_(out)
  N6: MBED2.pin10, Nokia_5110_LCD_Module1.D/C_(out)
  N7: MBED2.pin11, Nokia_5110_LCD_Module1.DN(MODI)_(out)
  N8: MBED2.pin12, Banggood_Display1.SDI
  N9: MBED2.pin13, Nokia_5110_LCD_Module1.SCLK_(out)
  N10: MBED2.pin22, Nokia_5110_LCD_Module1.SCE_(out)
  N11: MBED2.pin23, Banggood_Display1.DC
  N12: MBED2.pin24, Banggood_Display1.RST
  N13: MBED2.VOUT, R1.Pin_1, R2.Pin_1, Banggood_Display1.VCC, Banggood_Display1.LED, Nokia_5110_LCD_Module1.VCC_(out), Nokia_5110_LCD_Module1.LED_(out)

custom parts:
  Nokia 5110 LCD: Nokia 5110 Graphic 84*48 LCD module such as the Sparkfun LCD-10168 or the clones from Ebay. There is example code for the Arduino available from the Sparkfun site in https://learn.sparkfun.com/tutorials/graphic-lcd-hookup-guide This is a 3.3V device, if you are running it from a 5V micro you need a 5V tolorant level translator such as the 74ahc367 to protect the signal imputs. Rafa G. did a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
